// Digital circuit ALU.dig as structural Verilog
// Arithmetic Logical unit.
// Performs all arithmetic operations.
// Used for arithmetic processor instructions as well as for 
// calculating memory addresses.
// {{de Arithmetisch Logische Einheit. 
// Führt alle arithmetischen Operationen durch. 
// Wird sowohl für arithmetische Prozessorbefehle 
// als auch für die Berechnung der Adressen 
// bei der Speicheradressierung verwendet.}}
module ALU (
  input  [7:0] A,
  input  [7:0] B,
  input  [2:0] Op,
  input  Ci,
  input  RxC,
  output [7:0] Y,
  output [7:0] Flags
);

  wire Add, And, and_1_out, and_3_out, and_4_out, and_5_out, and_6_out, Cmpl, comparator_1_eq,
       comparator_1_gt, comparator_2_eq, comparator_2_gt, HC_sub, High_c_o, Low_c_o, LSR, lsr_1_co,
       multiplexer_1_out, Or, or_2_out, or_3_out, or_4_out, Sub, sub_1_c_o, unused, XOR;
  wire [3:0] High_s, Low_s;
  wire [7:0] and_2_out, lsr_1_do, or_1_out, sub_1_s, xor_1_out, xor_2_out;

  Decoder #(.Selector_Bits(3)) decoder_1 (
    .sel(Op), .out_0(Add), .out_1(Sub), .out_2(And), .out_3(LSR), .out_4(Cmpl), .out_5(Or), .out_6(XOR),
    .out_7(unused));
  Comparator #(.Bits(4)) comparator_1 (.a(B[3:0]), .b(A[3:0]), .gt(comparator_1_gt), .eq(comparator_1_eq));  // open: lt
  Multiplexer multiplexer_1 (.sel(RxC), .in_0(Ci), .in_1(Flags[0]), .out(multiplexer_1_out));
  and and_1 (and_1_out, comparator_1_eq, multiplexer_1_out);
  Add #(.Bits(4)) High (.a(A[7:4]), .b(B[7:4]), .c_i(Low_c_o), .s(High_s), .c_o(High_c_o));
  Add #(.Bits(4)) Low (.a(A[3:0]), .b(B[3:0]), .c_i(multiplexer_1_out), .s(Low_s), .c_o(Low_c_o));
  Sub #(.Bits(8)) sub_1 (.a(A), .b(B), .c_i(multiplexer_1_out), .s(sub_1_s), .c_o(sub_1_c_o));
  assign and_2_out = A & B;  // And and_2, 8 bits wide
  LSR lsr_1 (.Di(A), .Ci(multiplexer_1_out), .Do(lsr_1_do), .Co(lsr_1_co));
  Comparator #(.Bits(8)) comparator_2 (.a(B), .b(A), .gt(comparator_2_gt), .eq(comparator_2_eq));  // open: lt
  assign xor_1_out = A ^ {8{1'b1}};  // XOr xor_1, 8 bits wide
  assign or_1_out = A | B;  // Or or_1, 8 bits wide
  assign xor_2_out = A ^ B;  // XOr xor_2, 8 bits wide
  or or_2 (or_2_out, comparator_1_gt, and_1_out);
  and and_3 (and_3_out, comparator_2_eq, multiplexer_1_out);
  not not_1 (HC_sub, or_2_out);
  or or_3 (or_3_out, comparator_2_gt, and_3_out);
  or or_4 (or_4_out, A[3], B[3]);
  Multiplexer #(.Selector_Bits(3), .Bits(8)) multiplexer_2 (
    .sel(Op), .in_0({High_s, Low_s}), .in_1(sub_1_s), .in_2(and_2_out), .in_3(lsr_1_do), .in_4(xor_1_out),
    .in_5(or_1_out), .in_6(xor_2_out), .in_7({8{1'b0}}), .out({Flags[7], Y[6:0]}));
  and and_4 (and_4_out, Low_c_o, Add);
  and and_5 (and_5_out, HC_sub, Sub);
  and and_6 (and_6_out, or_4_out, And);
  Multiplexer #(.Selector_Bits(3)) multiplexer_3 (
    .sel(Op), .in_0(High_c_o), .in_1(or_3_out), .in_2(1'b0), .in_3(lsr_1_co), .in_4(1'b0), .in_5(1'b0),
    .in_6(1'b0), .in_7(1'b0), .out(Flags[0]));
  or or_5 (Flags[4], and_4_out, and_5_out, and_6_out);
  and and_7 (Flags[1], Sub, sub_1_c_o);
  Comparator #(.Bits(8)) comparator_3 (.a({Flags[7], Y[6:0]}), .b({8{1'b0}}), .eq(Flags[6]));  // open: gt, lt
  Parity parity_1 (.IN({Flags[7], Y[6:0]}), .P(Flags[2]));

  assign {Flags[5], Flags[3]} = 2'b00;
  assign Y[7] = Flags[7];

  // Other names for the same wires on the sheet: sel[2:0] = Op

  // Notes on the sheet:
  //   A: first operand
  //   {{de Erster Operand}}
  //   B: second operand
  //   {{de Zweiter Operand}}
  //   Op: selected operation
  //   {{de Operationswahl}}
  //   Y: result of the operation
  //   {{de Ergebnis der Operation}}
  //   Flags: Flag Signals (C,1,P,0,HC,0,Z,S)
  //   {{CPU Flags (C,1,P,0,HC,0,Z,S.}}
  //   Ci: carry input
  //   {{de Der Eingang für den Übertrag}}
  //   RxC: Register Cycle
  //   {{de Register Carry Cycle Command}}
  //   Functions
  //   0 = Add
  //   1 = Sub
  //   2 = AND
  //   3 = LSR
  //   4 = CMPL
  //   5 = OR
  //   6 = XOR
  //   7 = unused
  //   B + CY_in > A -> Carry
  //   Result
  //   Carry
  //   Half-Carry
endmodule
