// Digital circuit DAA.dig as structural Verilog
module DAA (
  input  [7:0] Reg,
  input  AC,
  input  CY,
  input  DAA,
  input  Reset,
  output [7:0] DAA_Const,
  output CY_DAA
);

  wire and_1_out, and_2_out, and_3_out, and_4_out, and_7_out, or_1_out, or_2_out, or_3_out, or_4_out,
       or_5_out;
  wire [1:0] and_5_out;
  wire [7:0] multiplexer_1_out;

  or or_1 (or_1_out, Reg[1], Reg[2]);
  and and_1 (and_1_out, or_1_out, Reg[3]);
  and and_2 (and_2_out, and_1_out, Reg[4]);
  or or_2 (or_2_out, and_2_out, Reg[5], Reg[6]);
  and and_3 (and_3_out, or_2_out, Reg[7]);
  or or_3 (or_3_out, and_3_out, CY);
  or or_4 (or_4_out, AC, and_1_out);
  and and_4 (and_4_out, and_1_out, and_3_out);
  and and_5 (and_5_out[0], or_4_out, DAA);
  and and_6 (and_5_out[1], or_3_out, DAA);
  or or_5 (or_5_out, and_4_out, or_3_out);
  Multiplexer #(.Selector_Bits(2), .Bits(8)) multiplexer_1 (
    .sel(and_5_out), .in_0({8{1'b0}}), .in_1(8'h6), .in_2(8'h60), .in_3(8'h66), .out(multiplexer_1_out));
  and and_7 (and_7_out, or_5_out, DAA);
  assign DAA_Const = DAA ? multiplexer_1_out : 8'bz;  // Driver driver_1
  RS_FF_AS rs_ff_as_1 (.S(and_7_out), .R(Reset), .Q(CY_DAA));  // open: nQ

  // Notes on the sheet:
  //   Reg: Register Input
  //   AC: Half Carry
  //   CY: Carry
  //   DAA: DAA instruction
  //   Reset: DAA instruction
  //   Comperator >= 10
endmodule
