// Digital circuit Flags.dig as structural Verilog
// CPU Flags handling.
module Flags (
  input  CLK,
  input  [7:0] Flags_ALU,
  input  CY_in,
  input  CY_DAA,
  input  Flags_in,
  input  Flags_out,
  input  [2:0] Flag_sel,
  input  Flag_BUS,
  input  CY_mode1,
  input  CY_mode2,
  input  CYtmp_in,
  input  CY_alu1,
  input  CY_alu2,
  input  [2:0] ALU_op,
  output [7:0] Flags,
  output AC_reg,
  output CY_reg,
  output C_ALU,
  output Flag,
  output [7:0] Flags_intern
);

  wire ADD_eq, and_1_out, nand_1_out, No_Carry_eq, not_1_out, or_1_out, register_1_q;
  wire [0:0] multiplexer_2_out;
  wire [7:0] multiplexer_1_out;

  or or_1 (or_1_out, Flags_ALU[0], Flags_ALU[1]);
  Comparator #(.Bits(3)) ADD (.a(ALU_op), .b(3'b000), .eq(ADD_eq));  // open: gt, lt
  Comparator #(.Bits(2)) No_Carry (.a({CY_in, Flags_in}), .b(2'b01), .eq(No_Carry_eq));  // open: gt, lt
  Multiplexer #(.Bits(8)) multiplexer_1 (.sel(Flag_BUS), .in_0(Flags_ALU), .in_1(Flags), .out(multiplexer_1_out));
  Register register_1 (.D(or_1_out), .C(CLK), .en(CYtmp_in), .Q(register_1_q));
  nand nand_1 (nand_1_out, ADD_eq, No_Carry_eq);
  not not_1 (not_1_out, multiplexer_1_out[0]);
  Multiplexer #(.Selector_Bits(2)) multiplexer_2 (
    .sel({CY_mode2, CY_mode1}), .in_0(multiplexer_1_out[0]), .in_1(not_1_out), .in_2(1'b1), .in_3(CY_DAA),
    .out(multiplexer_2_out[0]));
  Multiplexer #(.Selector_Bits(2)) multiplexer_3 (
    .sel({CY_alu2, CY_alu1}), .in_0(1'b0), .in_1(CY_reg), .in_2(1'b1), .in_3(register_1_q), .out(C_ALU));
  and and_1 (and_1_out, multiplexer_1_out[4], multiplexer_1_out[4]);
  Register Carry (.D(multiplexer_2_out[0]), .C(CLK), .en(CY_in), .Q(CY_reg));
  Register Parity (.D(multiplexer_1_out[2]), .C(CLK), .en(Flags_in), .Q(Flags_intern[2]));
  Register Half_Carry (.D(and_1_out), .C(CLK), .en(Flags_in), .Q(AC_reg));
  Register Zero (.D(multiplexer_1_out[6]), .C(CLK), .en(Flags_in), .Q(Flags_intern[6]));
  Register Signed (.D(multiplexer_1_out[7]), .C(CLK), .en(Flags_in), .Q(Flags_intern[7]));
  Multiplexer #(.Selector_Bits(3)) multiplexer_4 (
    .sel(Flag_sel), .in_0(CY_reg), .in_1(1'b1), .in_2(Flags_intern[2]), .in_3(1'b0), .in_4(AC_reg),
    .in_5(1'b0), .in_6(Flags_intern[6]), .in_7(Flags_intern[7]), .out(Flag));
  assign Flags = Flags_out ? {Flags_intern[7:6], 1'b0, AC_reg, 1'b0, Flags_intern[2], 1'b1, CY_reg} : 8'bz;  // Driver driver_1

  assign {Flags_intern[5:3], Flags_intern[1:0]} = {1'b0, AC_reg, 2'b01, CY_reg};

  // Notes on the sheet:
  //   Borrow (V) from ALU.
  //   Flg. <- Bus | ALU
  //   Temp. Carry
  //   for INX/DCX
  //   MUX Carry -> Reg.:
  //   00 : Pass
  //   01 : Complement
  //   02 : True
  //   03 : Keep
  //   MUX Carry ALU:
  //   00 : 0
  //   01 : Carry from Reg.
  //   02 : 1
  //   03 : Carry from Tmp.
endmodule
