// Digital circuit Parity.dig as structural Verilog
// 8 bit Even Parity Generator
module Parity (
  input  [7:0] IN,
  output P
);

  wire xor_1_out, xor_2_out, xor_3_out, xor_4_out, xor_5_out, xor_6_out, xor_7_out;

  xor xor_1 (xor_1_out, IN[0], IN[1]);
  xor xor_2 (xor_2_out, xor_1_out, IN[2]);
  xor xor_3 (xor_3_out, xor_2_out, IN[3]);
  xor xor_4 (xor_4_out, xor_3_out, IN[4]);
  xor xor_5 (xor_5_out, xor_4_out, IN[5]);
  xor xor_6 (xor_6_out, xor_5_out, IN[6]);
  xor xor_7 (xor_7_out, xor_6_out, IN[7]);
  not not_1 (P, xor_7_out);
endmodule
