// Digital circuit RSR.dig as structural Verilog
module RSR (
  input  [7:0] A,
  input  [7:0] B,
  input  C_in,
  input  RxC,
  output [7:0] Q_r,
  output [7:0] Q_L,
  output CY
);

  wire multiplexer_1_out;

  Multiplexer multiplexer_1 (.sel(RxC), .in_0(C_in), .in_1(CY), .out(multiplexer_1_out));
  Add #(.Bits(8)) add_1 (.a(A), .b(B), .c_i(multiplexer_1_out), .s(Q_L), .c_o(CY));
  LSR lsr_1 (.Di(A), .Ci(multiplexer_1_out), .Do(Q_r), .Co(CY));
endmodule
