// Digital circuit RST.dig as structural Verilog
// Push RST Addr. constant on BUS.
module RST (
  input  [7:0] Reg,
  input  RST,
  output [7:0] RST_Addr
);

  assign RST_Addr = RST ? {2'b00, Reg[5:3], 3'b000} : 8'bz;  // Driver driver_1

  // Notes on the sheet:
  //   Reg: Register Input
  //   RST: RST instruction
endmodule
