// Digital circuit Flash-Drive.dig as structural Verilog
module Flash_Drive (
  input  [7:0] ADDR_L,
  input  SYNC,
  input  IORQ,
  input  IN_nOUT,
  input  [7:0] BUS,
  output [1:0] Drive,
  output [23:0] Addr
);

  wire and_1_out, and_2_out, and_3_out, and_8_out, and_9_out, and_10_out, ATA_Sel, B_clk, comparator_1_eq,
       comparator_2_eq, D0, D1, D2, D3, DATA, DATA_Sel, Drive_t, IDESEC, or_1_out, OUT_Sync, R_EC, Read,
       Sector, Status_CMD, Track, Track2, Write;
  wire [3:2] Drive_q;
  wire [7:0] ERR_out;
  wire [26:24] Track2_q;

  and and_1 (and_1_out, IN_nOUT, Status_CMD, ATA_Sel);
  DipSwitch ERR (.out(ERR_out[0]));
  DipSwitch IDX (.out(ERR_out[1]));
  DipSwitch CORR (.out(ERR_out[2]));
  DipSwitch #(.dipDefault("true")) DRQ (.out(ERR_out[3]));
  DipSwitch DSC (.out(ERR_out[4]));
  DipSwitch DF (.out(ERR_out[5]));
  DipSwitch #(.dipDefault("true")) RDY (.out(ERR_out[6]));
  DipSwitch BUSY (.out(ERR_out[7]));
  and and_2 (and_2_out, Status_CMD, ATA_Sel);
  and and_3 (and_3_out, ~ADDR_L[7], ~ADDR_L[6], ~ADDR_L[5], ~ADDR_L[4], ADDR_L[3]);  // And
  assign BUS = and_1_out ? ERR_out : 8'bz;  // Driver driver_1
  Comparator #(.Bits(8)) comparator_1 (.a(BUS), .b(8'h20), .eq(comparator_1_eq));  // open: gt, lt
  Comparator #(.Bits(8)) comparator_2 (.a(BUS), .b(8'h30), .eq(comparator_2_eq));  // open: gt, lt
  and and_4 (ATA_Sel, IORQ, and_3_out);
  and and_5 (Read, and_2_out, comparator_1_eq);
  and and_6 (Write, and_2_out, comparator_2_eq);
  Decoder #(.Selector_Bits(3)) decoder_1 (
    .sel(ADDR_L[2:0]), .out_0(DATA), .out_1(R_EC), .out_2(IDESEC), .out_3(Sector), .out_4(Track),
    .out_5(Track2), .out_6(Drive_t), .out_7(Status_CMD));
  or or_1 (or_1_out, Read, Write);
  and and_7 (DATA_Sel, DATA, ATA_Sel);
  Register #(.Bits(4)) u_Drive (.D(BUS[7:4]), .C(OUT_Sync), .en(Drive_t), .Q({Drive_q, Drive}));
  Register #(.Bits(4)) u_Track2 (.D(BUS[3:0]), .C(OUT_Sync), .en(Track2), .Q({Track2_q, Addr[23]}));
  Register #(.Bits(8)) u_Track (.D(BUS), .C(OUT_Sync), .en(Track), .Q(Addr[22:15]));
  Register #(.Bits(8)) u_Sector (.D(BUS), .C(OUT_Sync), .en(Sector), .Q(Addr[14:7]));
  CounterPreset #(.Bits(7)) Bytes (
    .en(DATA_Sel), .C(B_clk), .dir(1'b0), .in({7{1'b0}}), .ld(1'b0), .clr(or_1_out), .out(Addr[6:0]));  // open: ovf
  and and_8 (and_8_out, DATA_Sel, ~IN_nOUT, SYNC);  // And
  and and_9 (and_9_out, DATA_Sel, IN_nOUT);
  and and_10 (and_10_out, DATA_Sel, SYNC);
  Decoder #(.Selector_Bits(2)) decoder_2 (.sel(Drive), .out_0(D0), .out_1(D1), .out_2(D2), .out_3(D3));
  or or_2 (B_clk, and_10_out, OUT_Sync);
  EEPROM #(.AddrBits(24), .Bits(8)) Drive_0 (.A(Addr), .CS(D0), .WE(and_8_out), .OE(and_9_out), .D(BUS));
  EEPROM #(.AddrBits(24), .Bits(8)) Drive_1 (.A(Addr), .CS(D1), .WE(and_8_out), .OE(and_9_out), .D(BUS));
  EEPROM #(.AddrBits(24), .Bits(8)) Drive_2 (.A(Addr), .CS(D2), .WE(and_8_out), .OE(and_9_out), .D(BUS));
  EEPROM #(.AddrBits(24), .Bits(8)) Drive_3 (.A(Addr), .CS(D3), .WE(and_8_out), .OE(and_9_out), .D(BUS));
  and and_11 (OUT_Sync, ~IN_nOUT, SYNC, ATA_Sel);  // And

  // Notes on the sheet:
  //   Drive I/O
  //   Drive Registers
  //   Drive Status
  //   Drive R/W
  //   ~CS1
  //   A2
  //   A1
  //   A0
  //   Drive Data
  //   Clear Byte counter for 
  //   Read or Write CMD.
  //   contents of Drive_0 (hex, n*v repeats v):
  //   31,0,2,cd,a8,0,d,a,43,50,2f,4d,20,4c,6f,61,64,65,72,20,31,2e,30,30
  //   ,3a,20,80,21,0,fa,11,2e,0,cd,72,0,cd,64,0,cd,a8,0,e2,13,3e,38
  //   ,bb,c2,21,0,21,0,ec,11,12,0,cd,72,0,cd,64,0,cd,a8,0,e4,13,3e,2e
  //   ,bb,c2,38,0,21,0,e4,11,2,0,cd,72,0,cd,64,0,cd,a8,0,e3,13,3e,12
  //   ,bb,c2,4f,0,c3,0,fa,76,6,0,db,8,77,23,4,78,fe,80,c2,66,0,c9,7b
  //   ,d3,b,7a,d3,c,af,d3,d,d3,e,3e,20,d3,f,db,f,7,da,81,0,7,d2,81,0
  //   ,f,f,f,d0,32,0,0,cd,9e,0,20,45,52,52,80,fb,c3,0,f8,cd,a8,0,d,a
  //   ,4c,4f,41,44,80,e3,7e,e6,7f,cd,b6,0,be,23,ca,a9,0,e3,c9,f5,db
  //   ,10,e6,2,ca,b7,0,f1,d3,11,c9,62*e5,c3,5c,e7,c3,58,e7,7f,0,16*20
  //   ,43,4f,50,59,52,49,47,48,54,20,28,43,29,20,31,39,37,39,2c,20,44
  //   ,49,47,49,54,41,4c,20,52,45,53,45,41,52,43,48,20,20,74*0,8,e4
  //   ,0,0,5f,e,2,c3,5,0,c5,cd,8c,e4,c1,c9,3e,d,cd,92,e4,3e,a,c3,92
  //   ,e4,3e,20,c3,92,e4,c5,cd,98,e4,e1,7e,b7,c8,23,e5,cd,8c,e4,e1,c3
  //   ,ac,e4,e,d,c3,5,0,5f,e,e,c3,5,0,cd,5,0,32,ee,eb,3c,c9,e,f,c3,c3
  //   ,e4,af,32,ed,eb,11,cd,eb,c3,cb,e4,e,10,c3,c3,e4,e,11,c3,c3,e4
  //   ,e,12,c3,c3,e4,11,cd,eb,c3,df,e4,e,13,c3,5,0,cd,5,0,b7,c9,e,14
  //   ,c3,f4,e4,11,cd,eb,c3,f9,e4,e,15,c3,f4,e4,e,16,c3,c3,e4,e,17,c3
  //   ,5,0,1e,ff,e,20,c3,5,0,cd,13,e5,4*87,21,ef,eb,b6,32,4,0,c9,3a
  //   ,ef,eb,32,4,0,c9,fe,61,d8,fe,7b,d0,e6,5f,c9,3a,ab,eb,b7,ca,96
  //   ,e5,3a,ef,eb,b7,3e,0,c4,bd,e4,11,ac,eb,cd,cb,e4,ca,96,e5,3a,bb
  //   ,eb,3d,32,cc,eb,11,ac,eb,cd,f9,e4,c2,96,e5,11,7,e4,21,80,0,6,80
  //   ,cd,42,e8,21,ba,eb,36,0,23,35,11,ac,eb,cd,da,e4,ca,96,e5,3a,ef
  //   ,eb,b7,c4,bd,e4,21,8,e4,cd,ac,e4,cd,c2,e5,ca,a7,e5,cd,dd,e5,c3
  //   ,82,e7,cd,dd,e5,cd,1a,e5,e,a,11,6,e4,cd,5,0,cd,29,e5,21,7,e4,46
  //   ,23,78,b7,ca,ba,e5,7e,cd,30,e5,77,5,c3,ab,e5,77,21,8,e4,22,88
  //   ,e4,c9,e,b,cd,5,0,b7,c8,e,1,cd,5,0,b7,c9,e,19,c3,5,0,11,80,0,e
  //   ,1a,c3,5,0,21,ab,eb,7e,b7,c8,36,0,af,cd,bd,e4,11,ac,eb,cd,ef,e4
  //   ,3a,ef,eb,c3,bd,e4,11,28,e7,21,0,ec,6,6,1a,be,c2,cf,e7,13,23,5
  //   ,c2,fd,e5,c9,cd,98,e4,2a,8a,e4,7e,fe,20,ca,22,e6,b7,ca,22,e6,e5
  //   ,cd,8c,e4,e1,23,c3,f,e6,3e,3f,cd,8c,e4,cd,98,e4,cd,dd,e5,c3,82
  //   ,e7,1a,b7,c8,fe,20,da,9,e6,c8,fe,3d,c8,fe,5f,c8,fe,2e,c8,fe,3a
  //   ,c8,fe,3b,c8,fe,3c,c8,fe,3e,c8,c9,1a,b7,c8,fe,20,c0,13,c3,4f,e6
  //   ,85,6f,d0,24,c9,3e,0,21,cd,eb,cd,59,e6,e5,e5,af,32,f0,eb,2a,88
  //   ,e4,eb,cd,4f,e6,eb,22,8a,e4,eb,e1,1a,b7,ca,89,e6,de,40,47,13,1a
  //   ,fe,3a,ca,90,e6,1b,3a,ef,eb,77,c3,96,e6,78,32,f0,eb,70,13,6,8
  //   ,cd,30,e6,ca,b9,e6,23,fe,2a,c2,a9,e6,36,3f,c3,ab,e6,77,13,5,c2
  //   ,98,e6,cd,30,e6,ca,c0,e6,13,c3,af,e6,23,36,20,5,c2,b9,e6,6,3,fe
  //   ,2e,c2,e9,e6,13,cd,30,e6,ca,e9,e6,23,fe,2a,c2,d9,e6,36,3f,c3,db
  //   ,e6,77,13,5,c2,c8,e6,cd,30,e6,ca,f0,e6,13,c3,df,e6,23,36,20,5
  //   ,c2,e9,e6,6,3,23,36,0,5,c2,f2,e6,eb,22,88,e4,e1,1,b,0,23,7e,fe
  //   ,3f,c2,9,e7,4,d,c2,1,e7,78,b7,c9,44,49,52,20,45,52,41,20,54,59
  //   ,50,45,53,41,56,45,52,45,4e,20,55,53,45,52,6*0,21,10,e7,e,0,79
  //   ,fe,6,d0,11,ce,eb,6,4,1a,be,c2,4f,e7,13,23,5,c2,3c,e7,1a,fe,20
  //   ,c2,54,e7,79,c9,23,5,c2,4f,e7,c,c3,33,e7,af,32,7,e4,31,ab,eb,c5
  //   ,79,4*1f,e6,f,5f,cd,15,e5,cd,b8,e4,32,ab,eb,c1,79,e6,f,32,ef,eb
  //   ,cd,bd,e4,3a,7,e4,b7,c2,98,e7,31,ab,eb,cd,98,e4,cd,d0,e5,c6,41
  //   ,cd,8c,e4,3e,3e,cd,8c,e4,cd,39,e5,11,80,0,cd,d8,e5,cd,d0,e5,32
  //   ,ef,eb,cd,5e,e6,c4,9,e6,3a,f0,eb,b7,c2,a5,ea,cd,2e,e7,21,c1,e7
  //   ,5f,16,0,19,19,7e,23,66,6f,e9,77,e8,1f,e9,5d,e9,ad,e9,10,ea,8e
  //   ,ea,a5,ea,21,f3,76,22,0,e4,21,0,e4,e9,1,df,e7,c3,a7,e4,52,45,41
  //   ,44,20,45,52,52,4f,52,0,1,f0,e7,c3,a7,e4,4e,4f,20,46,49,4c,45
  //   ,0,cd,5e,e6,3a,f0,eb,b7,c2,9,e6,21,ce,eb,1,b,0,7e,fe,20,ca,33
  //   ,e8,23,d6,30,fe,a,d2,9,e6,57,78,e6,e0,c2,9,e6,78,7,7,7,80,da,9
  //   ,e6,80,da,9,e6,82,da,9,e6,47,d,c2,8,e8,c9,7e,fe,20,c2,9,e6,23
  //   ,d,c2,33,e8,78,c9,6,3,7e,12,23,13,5,c2,42,e8,c9,21,80,0,81,cd
  //   ,59,e6,7e,c9,af,32,cd,eb,3a,f0,eb,b7,c8,3d,21,ef,eb,be,c8,c3,bd
  //   ,e4,3a,f0,eb,b7,c8,3d,21,ef,eb,be,c8,3a,ef,eb,c3,bd,e4,cd,5e,e6
  //   ,cd,54,e8,21,ce,eb,7e,fe,20,c2,8f,e8,6,b,36,3f,23,5,c2,88,e8,1e
  //   ,0,d5,cd,e9,e4,cc,ea,e7,ca,1b,e9,3a,ee,eb,f,f,f,e6,60,4f,3e,a
  //   ,cd,4b,e8,17,da,f,e9,d1,7b,1c,d5,e6,3,f5,c2,cc,e8,cd,98,e4,c5
  //   ,cd,d0,e5,c1,c6,41,cd,92,e4,3e,3a,cd,92,e4,c3,d4,e8,cd,a2,e4,3e
  //   ,3a,cd,92,e4,cd,a2,e4,6,1,78,cd,4b,e8,e6,7f,fe,20,c2,f9,e8,f1
  //   ,f5,fe,3,c2,f7,e8,3e,9,cd,4b,e8,e6,7f,fe,20,ca,e,e9,3e,20,cd,92
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  //   contents of Drive_1 (hex, n*v repeats v):
  //   120*e5,53,53,44,32,900*e5
  //   contents of Drive_2 (hex, n*v repeats v):
  //   120*e5,53,53,44,32,900*e5
  //   contents of Drive_3 (hex, n*v repeats v):
  //   120*e5,53,53,44,32,900*e5
endmodule
