// Digital circuit MEM-Async.dig as structural Verilog
module MEM_Async (
  input  [15:0] ADDR,
  input  MEM_RD,
  input  MEM_WR,
  input  SYNC,
  input  IORQ,
  input  IN_nOUT,
  input  RESET,
  output [7:0] BUS,
  output RAM
);

  wire A16, A17, A18, and_1_out, and_2_out, B16, B17, B18, comparator_2_eq, comparator_3_eq, MEM_IO, MEM_sel,
       not_1_out, not_2_out, RAM_EN, ROM_EN, S_addr0, S_addr1, S_addr2, S_addr3;
  wire [7:0] dipswitch_1_out, dipswitch_9_out, switchdt_1_p2;

  DipSwitch dipswitch_1 (.out(dipswitch_1_out[0]));
  DipSwitch dipswitch_2 (.out(dipswitch_1_out[1]));
  DipSwitch dipswitch_3 (.out(dipswitch_1_out[2]));
  DipSwitch #(.dipDefault("true")) dipswitch_4 (.out(dipswitch_1_out[3]));
  DipSwitch #(.dipDefault("true")) dipswitch_5 (.out(dipswitch_1_out[4]));
  DipSwitch dipswitch_6 (.out(dipswitch_1_out[5]));
  DipSwitch dipswitch_7 (.out(dipswitch_1_out[6]));
  DipSwitch dipswitch_8 (.out(dipswitch_1_out[7]));
  Comparator #(.Bits(8)) comparator_1 (.a(ADDR[7:0]), .b(dipswitch_1_out), .eq(MEM_sel));  // open: gt, lt
  or or_1 (MEM_IO, MEM_RD, MEM_WR);
  and and_1 (and_1_out, IN_nOUT, IORQ, MEM_IO, ~MEM_sel);  // And
  and and_2 (and_2_out, ~IN_nOUT, IORQ, SYNC, MEM_sel);  // And
  assign BUS = and_1_out ? {S_addr3, S_addr2, S_addr1, S_addr0, A18, A17, A16, RAM} : 8'bz;  // Driver driver_1
  D_FF_AS #(.Bits(8)) d_ff_as_1 (
    .Set(1'b0), .D(BUS), .C(and_2_out), .Clr(RESET),
    .Q({S_addr3, S_addr2, S_addr1, S_addr0, B18, B17, B16, RAM}));  // open: nQ
  RAMSinglePortSel #(.AddrBits(16), .isProgramMemory("true"), .Bits(8)) ramsingleportsel_1 (
    .A(ADDR), .CS(RAM_EN), .WE(MEM_WR), .OE(MEM_RD), .D(BUS));
  ROM #(.AddrBits(11), .Bits(8)) ROM (.A(ADDR[10:0]), .sel(ROM_EN), .D(BUS));
  // Probe on BUS
  // Probe on BUS
  Comparator #(.Bits(4)) comparator_2 (
    .a(ADDR[15:12]), .b({S_addr3, S_addr2, S_addr1, S_addr0}), .eq(comparator_2_eq));  // open: gt, lt
  // SwitchDT switchdt_1: pin names not known; wires that end beside it: 1'b0, switchdt_1_p2[7]
  // SwitchDT switchdt_2: pin names not known; wires that end beside it: RAM, 1'b0, switchdt_1_p2[6]
  // SwitchDT switchdt_3: pin names not known; wires that end beside it: ADDR[15], 1'b0, switchdt_1_p2[5]
  // SwitchDT switchdt_4: pin names not known; wires that end beside it: ADDR[14], 1'b0, switchdt_1_p2[4]
  // SwitchDT switchdt_5: pin names not known; wires that end beside it: ADDR[13], 1'b0, switchdt_1_p2[3]
  // SwitchDT switchdt_6: pin names not known; wires that end beside it: ADDR[12], 1'b0, switchdt_1_p2[2]
  // SwitchDT switchdt_7: pin names not known; wires that end beside it: ADDR[11], ADDR[10], switchdt_1_p2[1]
  // SwitchDT switchdt_8: pin names not known; wires that end beside it: 1'b0, ADDR[9], 1'b0, switchdt_1_p2[0]
  DipSwitch dipswitch_9 (.out(dipswitch_9_out[0]));
  DipSwitch dipswitch_10 (.out(dipswitch_9_out[1]));
  DipSwitch #(.dipDefault("true")) dipswitch_11 (.out(dipswitch_9_out[2]));
  DipSwitch #(.dipDefault("true")) dipswitch_12 (.out(dipswitch_9_out[3]));
  DipSwitch #(.dipDefault("true")) dipswitch_13 (.out(dipswitch_9_out[4]));
  DipSwitch #(.dipDefault("true")) dipswitch_14 (.out(dipswitch_9_out[5]));
  DipSwitch #(.dipDefault("true")) dipswitch_15 (.out(dipswitch_9_out[6]));
  DipSwitch dipswitch_16 (.out(dipswitch_9_out[7]));
  Multiplexer #(.Bits(3)) multiplexer_1 (
    .sel(comparator_2_eq), .in_0(3'b000), .in_1({B18, B17, B16}), .out({A18, A17, A16}));
  Comparator #(.Bits(8)) comparator_3 (.a(switchdt_1_p2), .b(dipswitch_9_out), .eq(comparator_3_eq));  // open: gt, lt
  not not_1 (not_1_out, MEM_IO);
  not not_2 (not_2_out, comparator_3_eq);
  nor nor_1 (ROM_EN, not_1_out, not_2_out);
  nor nor_2 (RAM_EN, not_1_out, comparator_3_eq);

  // Other names for the same wires on the sheet: mode = RAM; A_0 = ADDR[0]; ADDR_L[7:0] = ADDR[7:0]; A_1 = ADDR[1];
  //   A_2 = ADDR[2]; A_3 = ADDR[3]; A_4 = ADDR[4]; A_5 = ADDR[5]; A_6 = ADDR[6]; A_7 = ADDR[7];
  //   ADDR_H[7:0] = ADDR[15:8]

  // Notes on the sheet:
  //   MEM_WR: Write
  //   MEM SELECT
  //   MEM (0x18)
  //   MEM Status
  //   MEM CMD
  //   RAM/ROM
  //   ROM loads altmon.cim
  //   Common Memory Address and Bank Switching
  //   ROM Start Addr. for ROM/RAM Switching
  //   A15
  //   A9
  //   ~ROM_EN = ~MEM_IO | ~EQ
  //   ~RAM_EN = !MEM_IO | EQ
  //   Switch Mode ROM/RAM
  //   mode: 0 ROM, 1 RAM (force ROM/RAM)
  //   A15-A11 = 1, A10-A9 = 0 -> 0xF800 (ROM Start)
  //   lowest possible ROM start addr: 0x200 (A9)
endmodule
