// Digital circuit SAP-8080.dig as structural Verilog
module SAP_8080 (
  input  clk,
  input  nAuto_Manual,
  input  Reset,
  input  INT,
  input  [7:0] START,
  output INTE,
  output SYNC,
  output [15:0] ADDR,
  output INT_ack,
  output [7:0] DATA,
  output IORQ,
  output IN_nOUT
);

  wire A_in, A_out, AC_reg, Addr__Register_L_ovf, ALU_out, and_1_out, and_5_out, AR_en, ARH_in, ARL_in, B_in,
       B_out, button_1_out, C_ALU, C_in, C_out, CLK_t, CLR_I, CLR_PCR, CY_alu1, CY_alu2, CY_DAA, CY_in,
       CY_mode1, CY_mode2, CY_reg, CYtmp_in, D_in, D_out, DAA_out, decoder_1_out_0, decoder_1_out_1,
       decoder_1_out_3, E_in, E_out, EXEC, Flag, Flag_BUS, Flags_in, Flags_out, H_in, H_out, HLT, IC_clr,
       In_in, In_out, Int_clr, Int_dis, Int_ena, Int_pend, INTR, IO, IR_in, IR_out, L_in, L_out,
       mem_async_1_ram, monoflop_1_q, multiplexer_1_out, nCLK, not_1_out, or_1_out, Out_in, Out_out, PC_clr,
       PC_en, PC_in, PC_out, PR_in, PR_out, Program_Counter_ovf, r_MEM, rs_ff_as_2_q, RST_out, RxC, SP_dir,
       SP_en, SPH_in, SPH_out, SPL_in, SPL_out, Stackpointer_L_ovf, START_out, State_en, STOP, TMP1_en,
       TMP1_in, TMP1_out, TMP2_en, TMP2_in, TMP2_out, TMP_clr, uCdelay, w_MEM;
  wire [1:0] flash_drive_1_drive, N_State, State;
  wire [2:0] ALU_op, Flag_sel;
  wire [3:0] Input_Register_q, Input_Register_q_2, Output_Register_q, Output_Register_q_2,
       Program_Counter_out, Program_Counter_out_2, \µInstruction_Counter_out ;
  wire [4:0] In_sel, Out_sel;
  wire [7:0] A, alu_1_y, B_Register_q, C_Register_q, D_Register_q, E_Register_q, flags_1_flags_intern,
       Flags_ALU, H_Register_q, IR, L_Register_q, Page_Register_out, Stackpointer_H_out, Stackpointer_L_out,
       TMP1_Reg_q, TMP2_Reg_q;
  wire [23:0] flash_drive_1_addr;

  not not_1 (not_1_out, EXEC);
  TTY tty_1 (.ADDR_L(ADDR[7:0]), .SYNC(SYNC), .IORQ(IORQ), .IN_nOUT(IN_nOUT), .BUS(DATA));
  Flash_Drive flash_drive_1 (
    .ADDR_L(ADDR[7:0]), .SYNC(SYNC), .IORQ(IORQ), .IN_nOUT(IN_nOUT), .BUS(DATA), .Drive(flash_drive_1_drive),
    .Addr(flash_drive_1_addr));
  MEM_Async mem_async_1 (
    .ADDR(ADDR), .MEM_RD(r_MEM), .MEM_WR(w_MEM), .SYNC(SYNC), .IORQ(IORQ), .IN_nOUT(IN_nOUT), .RESET(Reset),
    .BUS(DATA), .RAM(mem_async_1_ram));
  DAA daa_1 (.Reg(A), .AC(AC_reg), .CY(CY_reg), .DAA(DAA_out), .Reset(not_1_out), .DAA_Const(DATA), .CY_DAA(CY_DAA));
  RST rst_1 (.Reg(IR), .RST(RST_out), .RST_Addr(DATA));
  assign DATA = START_out ? START : 8'bz;  // Driver driver_1
  // Probe Drive on flash_drive_1_drive
  // Probe Address on flash_drive_1_addr
  LED RAM (.in(mem_async_1_ram));
  Register #(.Bits(8)) TMP1_Reg (.D(DATA), .C(CLK_t), .en(TMP1_en), .Q(TMP1_Reg_q));
  Register #(.Bits(8)) A_Register (.D(DATA), .C(CLK_t), .en(A_in), .Q(A));
  Register #(.Bits(8)) TMP2_Reg (.D(DATA), .C(CLK_t), .en(TMP2_en), .Q(TMP2_Reg_q));
  Register #(.Bits(8)) B_Register (.D(DATA), .C(CLK_t), .en(B_in), .Q(B_Register_q));
  Register #(.Bits(8)) D_Register (.D(DATA), .C(CLK_t), .en(D_in), .Q(D_Register_q));
  Register #(.Bits(8)) H_Register (.D(DATA), .C(CLK_t), .en(H_in), .Q(H_Register_q));
  CounterPreset #(.Bits(8), .isProgramCounter("true")) Addr__Register_L (
    .en(AR_en), .C(CLK_t), .dir(1'b0), .in(DATA), .ld(ARL_in), .clr(1'b0), .out(ADDR[7:0]),
    .ovf(Addr__Register_L_ovf));
  CounterPreset #(.Bits(8), .isProgramCounter("true")) Addr__Register_H (
    .en(Addr__Register_L_ovf), .C(CLK_t), .dir(1'b0), .in(DATA), .ld(ARH_in), .clr(1'b0), .out(ADDR[15:8]));  // open: ovf
  Register #(.Bits(8)) Output_Register (.D(DATA), .C(CLK_t), .en(Out_in), .Q({Output_Register_q_2, Output_Register_q}));
  Register #(.Bits(8)) Input_Register (.D(DATA), .C(CLK_t), .en(In_in), .Q({Input_Register_q_2, Input_Register_q}));
  assign DATA = A_out ? A : 8'bz;  // Driver driver_2
  Seven_Seg_Hex seven_seg_hex_1 (.d(Output_Register_q), .dp(1'b0));
  Seven_Seg_Hex seven_seg_hex_2 (.d(Output_Register_q_2), .dp(1'b0));
  Seven_Seg_Hex seven_seg_hex_3 (.d(ADDR[15:12]), .dp(1'b0));
  assign DATA = Out_out ? {Output_Register_q_2, Output_Register_q} : 8'bz;  // Driver driver_3
  ALU alu_1 (.A(TMP1_Reg_q), .B(TMP2_Reg_q), .Op(ALU_op), .Y(alu_1_y), .Flags(Flags_ALU), .Ci(C_ALU), .RxC(RxC));
  Seven_Seg_Hex seven_seg_hex_4 (.d(ADDR[7:4]), .dp(1'b0));
  Seven_Seg_Hex seven_seg_hex_5 (.d(ADDR[11:8]), .dp(1'b0));
  Seven_Seg_Hex seven_seg_hex_6 (.d(Input_Register_q), .dp(1'b0));
  Seven_Seg_Hex seven_seg_hex_7 (.d(Input_Register_q_2), .dp(1'b0));
  Seven_Seg_Hex seven_seg_hex_8 (.d(ADDR[3:0]), .dp(1'b0));
  assign DATA = In_out ? {Input_Register_q_2, Input_Register_q} : 8'bz;  // Driver driver_4
  LED S (.in(Flags_ALU[7]));
  assign DATA = TMP1_out ? TMP1_Reg_q : 8'bz;  // Driver driver_5
  assign DATA = ALU_out ? alu_1_y : 8'bz;  // Driver driver_6
  LED Z (.in(Flags_ALU[6]));
  assign DATA = TMP2_out ? TMP2_Reg_q : 8'bz;  // Driver driver_7
  assign DATA = B_out ? B_Register_q : 8'bz;  // Driver driver_8
  assign DATA = D_out ? D_Register_q : 8'bz;  // Driver driver_9
  assign DATA = H_out ? H_Register_q : 8'bz;  // Driver driver_10
  LED AC (.in(Flags_ALU[4]));
  Register #(.Bits(8)) C_Register (.D(DATA), .C(CLK_t), .en(C_in), .Q(C_Register_q));
  Register #(.Bits(8)) E_Register (.D(DATA), .C(CLK_t), .en(E_in), .Q(E_Register_q));
  Register #(.Bits(8)) L_Register (.D(DATA), .C(CLK_t), .en(L_in), .Q(L_Register_q));
  Flags flags_1 (
    .CLK(CLK_t), .Flags_ALU(Flags_ALU), .CY_in(CY_in), .CY_DAA(CY_DAA), .Flags_in(Flags_in),
    .Flags_out(Flags_out), .Flag_sel(Flag_sel), .Flag_BUS(Flag_BUS), .CY_mode1(CY_mode1),
    .CY_mode2(CY_mode2), .CYtmp_in(CYtmp_in), .CY_alu1(CY_alu1), .CY_alu2(CY_alu2), .ALU_op(ALU_op),
    .Flags(DATA), .AC_reg(AC_reg), .CY_reg(CY_reg), .C_ALU(C_ALU), .Flag(Flag),
    .Flags_intern(flags_1_flags_intern));
  LED S_2 (.in(flags_1_flags_intern[7]));
  LED P (.in(Flags_ALU[2]));
  LED V (.in(Flags_ALU[1]));
  LED AC_2 (.in(flags_1_flags_intern[4]));
  LED Z_2 (.in(flags_1_flags_intern[6]));
  LED C (.in(Flags_ALU[0]));
  assign DATA = C_out ? C_Register_q : 8'bz;  // Driver driver_11
  assign DATA = E_out ? E_Register_q : 8'bz;  // Driver driver_12
  assign DATA = L_out ? L_Register_q : 8'bz;  // Driver driver_13
  LED C_2 (.in(flags_1_flags_intern[0]));
  LED P_2 (.in(flags_1_flags_intern[2]));
  PullDown #(.Bits(8)) pulldown_1 (.out(DATA));
  CounterPreset #(.Bits(8), .isProgramCounter("true")) Program_Counter (
    .en(PC_en), .C(CLK_t), .dir(1'b0), .in(DATA), .ld(PC_in), .clr(PC_clr),
    .out({Program_Counter_out_2, Program_Counter_out}), .ovf(Program_Counter_ovf));
  CounterPreset #(.Bits(8), .isProgramCounter("true")) Page_Register (
    .en(Program_Counter_ovf), .C(CLK_t), .dir(1'b0), .in(DATA), .ld(PR_in), .clr(PC_clr),
    .out(Page_Register_out));  // open: ovf
  Register #(.Bits(8)) Instr__Register (.D(DATA), .C(CLK_t), .en(IR_in), .Q(IR));
  CounterPreset #(.Bits(8), .isProgramCounter("true")) Stackpointer_L (
    .en(SP_en), .C(CLK_t), .dir(SP_dir), .in(DATA), .ld(SPL_in), .clr(1'b0), .out(Stackpointer_L_out),
    .ovf(Stackpointer_L_ovf));
  CounterPreset #(.Bits(8), .isProgramCounter("true")) Stackpointer_H (
    .en(Stackpointer_L_ovf), .C(CLK_t), .dir(SP_dir), .in(DATA), .ld(SPH_in), .clr(1'b0),
    .out(Stackpointer_H_out));  // open: ovf
  Seven_Seg_Hex seven_seg_hex_9 (.d(DATA[7:4]), .dp(1'b0));
  assign DATA = SPL_out ? Stackpointer_L_out : 8'bz;  // Driver driver_14
  assign DATA = SPH_out ? Stackpointer_H_out : 8'bz;  // Driver driver_15
  Seven_Seg_Hex seven_seg_hex_10 (.d(DATA[3:0]), .dp(1'b0));
  Seven_Seg_Hex seven_seg_hex_11 (.d(Program_Counter_out), .dp(1'b0));
  Seven_Seg_Hex seven_seg_hex_12 (.d(Program_Counter_out_2), .dp(1'b0));
  Seven_Seg_Hex seven_seg_hex_13 (.d(Page_Register_out[3:0]), .dp(1'b0));
  Seven_Seg_Hex seven_seg_hex_14 (.d(Page_Register_out[7:4]), .dp(1'b0));
  Seven_Seg_Hex seven_seg_hex_15 (.d(IR[3:0]), .dp(1'b0));
  Seven_Seg_Hex seven_seg_hex_16 (.d(IR[7:4]), .dp(1'b0));
  Seven_Seg_Hex seven_seg_hex_17 (.d(Stackpointer_H_out[7:4]), .dp(1'b0));
  assign DATA = PC_out ? {Program_Counter_out_2, Program_Counter_out} : 8'bz;  // Driver driver_16
  assign DATA = PR_out ? Page_Register_out : 8'bz;  // Driver driver_17
  assign DATA = IR_out ? IR : 8'bz;  // Driver driver_18
  Seven_Seg_Hex seven_seg_hex_18 (.d(Stackpointer_L_out[7:4]), .dp(1'b0));
  Seven_Seg_Hex seven_seg_hex_19 (.d(Stackpointer_H_out[3:0]), .dp(1'b0));
  Seven_Seg_Hex seven_seg_hex_20 (.d(Stackpointer_L_out[3:0]), .dp(1'b0));
  Monoflop #(.timerDelay(2)) monoflop_1 (.C(1'b1), .R(1'b0), .Q(monoflop_1_q), .nQ(uCdelay));
  and and_1 (and_1_out, HLT, ~INTR);  // And
  CounterPreset #(.Bits(2), .isProgramCounter("true")) u_State (
    .en(1'b0), .C(nCLK), .dir(1'b0), .in(N_State), .ld(State_en), .clr(or_1_out), .out(State));  // open: ovf
  or or_1 (or_1_out, PC_clr, monoflop_1_q);
  Button button_1 (.out(button_1_out));
  Counter #(.Bits(4)) \u_µInstruction_Counter  (
    .en(uCdelay), .C(nCLK), .clr(IC_clr), .out(\µInstruction_Counter_out ));  // open: ovf
  or or_2 (PC_clr, Reset, CLR_PCR);
  or or_3 (IC_clr, Reset, CLR_I);
  and and_2 (STOP, ~Reset, and_1_out);  // And
  Decoder #(.Selector_Bits(2)) decoder_1 (
    .sel(State), .out_0(decoder_1_out_0), .out_1(decoder_1_out_1), .out_2(EXEC), .out_3(decoder_1_out_3));
  Multiplexer multiplexer_1 (.sel(nAuto_Manual), .in_0(clk), .in_1(button_1_out), .out(multiplexer_1_out));
  Seven_Seg_Hex seven_seg_hex_21 (.d(\µInstruction_Counter_out ), .dp(1'b0));
  ROM #(.AddrBits(16), .Bits(8)) Microcode (
    .A({State, Int_pend, Flag, IR, \µInstruction_Counter_out }), .sel(1'b1),
    .D({Out_sel[0], In_sel, CLR_PCR, PC_en}));
  ROM #(.AddrBits(16), .Bits(8)) Microcode_2 (
    .A({State, Int_pend, Flag, IR, \µInstruction_Counter_out }), .sel(1'b1),
    .D({CY_alu1, ALU_op, Out_sel[4:1]}));
  ROM #(.AddrBits(16), .Bits(8)) Microcode_3 (
    .A({State, Int_pend, Flag, IR, \µInstruction_Counter_out }), .sel(1'b1),
    .D({Flag_sel, SP_dir, SP_en, SYNC, CYtmp_in, CY_alu2}));
  ROM #(.AddrBits(16), .Bits(8)) Microcode_4 (
    .A({State, Int_pend, Flag, IR, \µInstruction_Counter_out }), .sel(1'b1),
    .D({CLR_I, RxC, N_State, CY_in, Flags_in, Flags_out, Flag_BUS}));
  LED Init (.in(decoder_1_out_0));
  LED Fetch (.in(decoder_1_out_1));
  LED u_Exec (.in(EXEC));
  LED Interrupt (.in(decoder_1_out_3));
  and and_3 (CLK_t, multiplexer_1_out, ~STOP);  // And
  or or_4 (IORQ, IN_nOUT, IO);
  not not_2 (nCLK, CLK_t);
  LED led_1 (.in(PC_en));
  LED led_2 (.in(CLR_PCR));
  LED led_3 (.in(In_sel[0]));
  LED led_4 (.in(In_sel[1]));
  LED led_5 (.in(In_sel[2]));
  LED led_6 (.in(In_sel[3]));
  LED led_7 (.in(In_sel[4]));
  LED led_8 (.in(Out_sel[0]));
  LED led_9 (.in(Out_sel[1]));
  LED led_10 (.in(Out_sel[2]));
  LED led_11 (.in(Out_sel[3]));
  LED led_12 (.in(Out_sel[4]));
  LED led_13 (.in(ALU_op[0]));
  LED led_14 (.in(ALU_op[1]));
  LED led_15 (.in(ALU_op[2]));
  LED led_16 (.in(CY_alu1));
  LED led_17 (.in(CY_alu2));
  LED led_18 (.in(CYtmp_in));
  LED led_19 (.in(SYNC));
  LED led_20 (.in(SP_en));
  LED led_21 (.in(SP_dir));
  LED led_22 (.in(Flag_sel[0]));
  LED led_23 (.in(Flag_sel[1]));
  LED led_24 (.in(Flag_sel[2]));
  RS_FF_AS rs_ff_as_1 (.S(Int_ena), .R(Int_dis), .Q(INTE));  // open: nQ
  RS_FF_AS rs_ff_as_2 (.S(INT), .R(Int_clr), .Q(rs_ff_as_2_q));  // open: nQ
  LED u_INTE (.in(INTE));
  and and_4 (INTR, INTE, rs_ff_as_2_q, EXEC);
  Decoder #(.Selector_Bits(5)) decoder_2 (
    .sel(In_sel), .out_1(IR_in), .out_2(IO), .out_3(A_in), .out_4(B_in), .out_5(C_in), .out_6(D_in),
    .out_7(E_in), .out_8(H_in), .out_9(L_in), .out_10(TMP1_in), .out_11(TMP2_in), .out_12(ARL_in),
    .out_13(ARH_in), .out_14(SPL_in), .out_15(SPH_in), .out_16(AR_en), .out_17(Out_in), .out_18(In_in),
    .out_19(PC_in), .out_20(PR_in), .out_21(w_MEM), .out_27(HLT), .out_28(CY_mode1), .out_29(Int_ena),
    .out_30(Int_dis), .out_31(State_en));  // open: out_0, out_22, out_23, out_24, out_25, out_26
  or or_5 (TMP1_en, TMP1_in, TMP_clr);
  or or_6 (TMP2_en, TMP_clr, TMP2_in);
  LED led_25 (.in(Flag_BUS));
  LED led_26 (.in(Flags_out));
  LED led_27 (.in(Flags_in));
  LED led_28 (.in(CY_in));
  LED led_29 (.in(N_State[0]));
  LED led_30 (.in(N_State[1]));
  LED led_31 (.in(RxC));
  LED led_32 (.in(CLR_I));
  and and_5 (and_5_out, INTR, CLK_t);
  Decoder #(.Selector_Bits(5)) decoder_3 (
    .sel(Out_sel), .out_1(PC_out), .out_2(PR_out), .out_3(A_out), .out_4(B_out), .out_5(C_out),
    .out_6(D_out), .out_7(E_out), .out_8(H_out), .out_9(L_out), .out_10(TMP1_out), .out_11(TMP2_out),
    .out_12(SPL_out), .out_13(SPH_out), .out_14(ALU_out), .out_15(r_MEM), .out_16(In_out), .out_17(IR_out),
    .out_18(RST_out), .out_19(START_out), .out_20(IN_nOUT), .out_21(Out_out), .out_27(INT_ack),
    .out_28(CY_mode2), .out_29(DAA_out), .out_30(TMP_clr), .out_31(Int_clr));  // open: out_0, out_22, out_23, out_24, out_25, out_26
  D_FF_AS Interrupt_Flag (.Set(and_5_out), .D(Int_pend), .C(CLK_t), .Clr(Int_clr), .Q(Int_pend));  // open: nQ

  // Other names for the same wires on the sheet: Addr_L[7:0] = ADDR[7:0]

  // Notes on the sheet:
  //   clk: Hz: 2147483647
  //   START: default 248
  //   I/O
  //   Misc.
  //   Datapath
  //   Out
  //   Address
  //   In
  //   BUS
  //   Stackpointer
  //   Control Logic
  //   Cear Halt if Interrupt.
  //   Clock
  //   Init delay.
  //   Used counter 
  //   because generic
  //   Reg has no CLR.
  //   contents of Microcode (hex, n*v repeats v):
  //   21,1a,14*0,21,1a,14*0,21,1a,14*0,21,1a,14*0,21,1a,14*0,21,1a,14*0
  //   ,21,1a,14*0,21,1a,14*0,21,1a,14*0,21,1a,14*0,21,1a,14*0,21,1a
  //   ,14*0,21,1a,14*0,21,1a,14*0,21,1a,14*0,21,1a,14*0,21,1a,14*0,21
  //   ,1a,14*0,21,1a,14*0,21,1a,14*0,21,1a,14*0,21,1a,14*0,21,1a,14*0
  //   ,21,1a,14*0,21,1a,14*0,21,1a,14*0,21,1a,14*0,21,1a,14*0,21,1a
  //   ,14*0,21,1a,14*0,21,1a,14*0,21,1a,14*0,21,1a,14*0,21,1a,14*0,21
  //   ,1a,14*0,21,1a,14*0,21,1a,14*0,21,1a,14*0,21,1a,14*0,21,1a,14*0
  //   ,21,1a,14*0,21,1a,14*0,21,1a,14*0,21,1a,14*0,21,1a,14*0,21,1a
  //   ,14*0,21,1a,14*0,21,1a,14*0,21,1a,14*0,21,1a,14*0,21,1a,14*0,21
  //   ,1a,14*0,21,1a,14*0,21,1a,14*0,21,1a,14*0,21,1a,14*0,21,1a,14*0
  //   ,21,1a,14*0,21,1a,14*0,21,1a,14*0,21,1a,14*0,21,1a,14*0,21,1a
  //   ,14*0,21,1a,14*0,21,1a,14*0,21,1a,14*0,21,1a,14*0,21,1a,14*0,21
  //   ,1a,14*0,21,1a,14*0,21,1a,14*0,21,1a,14*0,21,1a,14*0,21,1a,14*0
  //   ,21,1a,14*0,21,1a,14*0,21,1a,14*0,21,1a,14*0,21,1a,14*0,21,1a
  //   ,14*0,21,1a,14*0,21,1a,14*0,21,1a,14*0,21,1a,14*0,21,1a,14*0,21
  //   ,1a,14*0,21,1a,14*0,21,1a,14*0,21,1a,14*0,21,1a,14*0,21,1a,14*0
  //   ,21,1a,14*0,21,1a,14*0,21,1a,14*0,21,1a,14*0,21,1a,14*0,21,1a
  //   ,14*0,21,1a,14*0,21,1a,14*0,21,1a,14*0,21,1a,14*0,21,1a,14*0,21
  //   ,1a,14*0,21,1a,14*0,21,1a,14*0,21,1a,14*0,21,1a,14*0,21,1a,14*0
  //   ,21,1a,14*0,21,1a,14*0,21,1a,14*0,21,1a,14*0,21,1a,14*0,21,1a
  //   ,14*0,21,1a,14*0,21,1a,14*0,21,1a,14*0,21,1a,14*0,21,1a,14*0,21
  //   ,1a,14*0,21,1a,14*0,21,1a,14*0,21,1a,14*0,21,1a,14*0,21,1a,14*0
  //   ,21,1a,14*0,21,1a,14*0,21,1a,14*0,21,1a,14*0,21,1a,14*0,21,1a
  //   ,14*0,21,1a,14*0,21,1a,14*0,21,1a,14*0,21,1a,14*0,21,1a,14*0,21
  //   ,1a,14*0,21,1a,14*0,21,1a,14*0,21,1a,14*0,21,1a,14*0,21,1a,14*0
  //   ,21,1a,14*0,21,1a,14*0,21,1a,14*0,21,1a,14*0,21,1a,14*0,21,1a
  //   ,14*0,21,1a,14*0,21,1a,14*0,21,1a,14*0,21,1a,14*0,21,1a,14*0,21
  //   ,1a,14*0,21,1a,14*0,21,1a,14*0,21,1a,14*0,21,1a,14*0,21,1a,14*0
  //   ,21,1a,14*0,21,1a,14*0,21,1a,14*0,21,1a,14*0,21,1a,14*0,21,1a
  //   ,14*0,21,1a,14*0,21,1a,14*0,21,1a,14*0,21,1a,14*0,21,1a,14*0,21
  //   ,1a,14*0,21,1a,14*0,21,1a,14*0,21,1a,14*0,21,1a,14*0,21,1a,14*0
  //   ,21,1a,8480,800000,12*0,21,1a,14*0,21,1a,14*0,21,1a,14*0,21,1a
  //   ,8c80,800000,12*0,21,1a,14*0,21,1a,14*0,21,1a,14*0,21,1a,14*0
  //   ,21,1a,14*0,21,1a,14*0,21,1a,14*0,21,1a,14*0,21,1a,14*0,21,1a
  //   ,14*0,21,1a,14*0,21,1a,21,4012,800000,11*0,21,1a,14*0,21,1a,14*0
  //   ,21,1a,14*0,21,1a,2,800000,12*0,21,1a,14*0,21,1a,14*0,21,1a,14*0
  //   ,21,1a,800000,13*0,21,1a,14*0,21,1a,14*0,21,1a,14*0,21,1a,14*0
  //   ,21,1a,14*0,21,1a,14*0,21,1a,14*0,21,1a,14*0,21,1a,14*0,21,1a
  //   ,14*0,21,1a,14*0,21,1a,14*0,21,1a,14*0,21,1a,14*0,21,1a,14*0,21
  //   ,1a,14*0,21,1a,14*0,21,1a,14*0,21,1a,14*0,21,1a,14*0,21,1a,14*0
  //   ,21,1a,14*0,21,1a,14*0,21,1a,21,92,800000,11*0,21,1a,14*0,21,1a
  //   ,14*0,21,1a,14*0,21,1a,21,212,800000,11*0,21,1a,14*0,21,1a,14*0
  //   ,21,1a,14*0,21,1a,2040,800000,12*0,21,1a,14*0,21,1a,14*0,21,1a
  //   ,14*0,21,1a,14*0,21,1a,14*0,21,1a,14*0,21,1a,14*0,21,1a,14*0,21
  //   ,1a,14*0,21,1a,14*0,21,1a,14*0,21,1a,14*0,21,1a,14*0,21,1a,14*0
  //   ,21,1a,14*0,21,1a,14*0,21,1a,14*0,21,1a,14*0,21,1a,14*0,21,1a
  //   ,14*0,21,1a,14*0,21,1a,c00000,13*0,21,1a,200000,13*0,21,1a,14*0
  //   ,21,1a,14*0,21,1a,14*0,21,1a,14*0,21,1a,14*0,21,1a,14*0,21,1a
  //   ,14*0,21,1a,14*0,21,1a,14*0,21,1a,14*0,21,1a,14*0,21,1a,14*0,21
  //   ,1a,14*0,21,1a,14*0,21,1a,14*0,21,1a,14*0,21,1a,14*0,21,1a,14*0
  //   ,21,1a,14*0,21,1a,14*0,21,1a,14*0,21,1a,14*0,21,1a,14*0,21,1a
  //   ,14*0,21,1a,14*0,21,1a,14*0,21,1a,14*0,21,1a,14*0,21,1a,14*0,21
  //   ,1a,14*0,21,1a,14*0,21,1a,14*0,21,1a,14*0,21,1a,14*0,21,1a,14*0
  //   ,21,1a,14*0,21,1a,14*0,21,1a,14*0,21,1a,14*0,21,1a,14*0,21,1a
  //   ,14*0,21,1a,14*0,21,1a,14*0,21,1a,14*0,21,1a,14*0,21,1a,14*0,21
  //   ,1a,14*0,21,1a,14*0,21,1a,14*0,21,1a,14*0,21,1a,14*0,21,1a,14*0
  //   ,21,1a,14*0,21,1a,14*0,21,1a,14*0,21,1a,14*0,21,1a,14*0,21,1a
  //   ,14*0,21,1a,14*0,21,1a,14*0,21,1a,14*0,21,1a,14*0,21,1a,14*0,21
  //   ,1a,14*0,21,1a,14*0,21,1a,14*0,21,1a,14*0,21,1a,14*0,21,1a,14*0
  //   ,21,1a,14*0,21,1a,14*0,21,1a,14*0,21,1a,14*0,21,1a,14*0,21,1a
  //   ,14*0,21,1a,14*0,21,1a,14*0,21,1a,14*0,21,1a,14*0,21,1a,14*0,21
  //   ,1a,14*0,21,1a,14*0,21,1a,14*0,21,1a,14*0,21,1a,14*0,21,1a,14*0
  //   ,21,1a,14*0,21,1a,14*0,21,1a,14*0,21,1a,14*0,21,1a,14*0,21,1a
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  //   contents of Microcode_2 (hex, n*v repeats v):
  //   21,1a,14*0,21,1a,14*0,21,1a,14*0,21,1a,14*0,21,1a,14*0,21,1a,14*0
  //   ,21,1a,14*0,21,1a,14*0,21,1a,14*0,21,1a,14*0,21,1a,14*0,21,1a
  //   ,14*0,21,1a,14*0,21,1a,14*0,21,1a,14*0,21,1a,14*0,21,1a,14*0,21
  //   ,1a,14*0,21,1a,14*0,21,1a,14*0,21,1a,14*0,21,1a,14*0,21,1a,14*0
  //   ,21,1a,14*0,21,1a,14*0,21,1a,14*0,21,1a,14*0,21,1a,14*0,21,1a
  //   ,14*0,21,1a,14*0,21,1a,14*0,21,1a,14*0,21,1a,14*0,21,1a,14*0,21
  //   ,1a,14*0,21,1a,14*0,21,1a,14*0,21,1a,14*0,21,1a,14*0,21,1a,14*0
  //   ,21,1a,14*0,21,1a,14*0,21,1a,14*0,21,1a,14*0,21,1a,14*0,21,1a
  //   ,14*0,21,1a,14*0,21,1a,14*0,21,1a,14*0,21,1a,14*0,21,1a,14*0,21
  //   ,1a,14*0,21,1a,14*0,21,1a,14*0,21,1a,14*0,21,1a,14*0,21,1a,14*0
  //   ,21,1a,14*0,21,1a,14*0,21,1a,14*0,21,1a,14*0,21,1a,14*0,21,1a
  //   ,14*0,21,1a,14*0,21,1a,14*0,21,1a,14*0,21,1a,14*0,21,1a,14*0,21
  //   ,1a,14*0,21,1a,14*0,21,1a,14*0,21,1a,14*0,21,1a,14*0,21,1a,14*0
  //   ,21,1a,14*0,21,1a,14*0,21,1a,14*0,21,1a,14*0,21,1a,14*0,21,1a
  //   ,14*0,21,1a,14*0,21,1a,14*0,21,1a,14*0,21,1a,14*0,21,1a,14*0,21
  //   ,1a,14*0,21,1a,14*0,21,1a,14*0,21,1a,14*0,21,1a,14*0,21,1a,14*0
  //   ,21,1a,14*0,21,1a,14*0,21,1a,14*0,21,1a,14*0,21,1a,14*0,21,1a
  //   ,14*0,21,1a,14*0,21,1a,14*0,21,1a,14*0,21,1a,14*0,21,1a,14*0,21
  //   ,1a,14*0,21,1a,14*0,21,1a,14*0,21,1a,14*0,21,1a,14*0,21,1a,14*0
  //   ,21,1a,14*0,21,1a,14*0,21,1a,14*0,21,1a,14*0,21,1a,14*0,21,1a
  //   ,14*0,21,1a,14*0,21,1a,14*0,21,1a,14*0,21,1a,14*0,21,1a,14*0,21
  //   ,1a,14*0,21,1a,14*0,21,1a,14*0,21,1a,14*0,21,1a,14*0,21,1a,14*0
  //   ,21,1a,14*0,21,1a,14*0,21,1a,14*0,21,1a,14*0,21,1a,14*0,21,1a
  //   ,14*0,21,1a,14*0,21,1a,14*0,21,1a,14*0,21,1a,14*0,21,1a,14*0,21
  //   ,1a,14*0,21,1a,14*0,21,1a,14*0,21,1a,14*0,21,1a,14*0,21,1a,14*0
  //   ,21,1a,14*0,21,1a,14*0,21,1a,14*0,21,1a,14*0,21,1a,14*0,21,1a
  //   ,14*0,21,1a,14*0,21,1a,14*0,21,1a,14*0,21,1a,14*0,21,1a,14*0,21
  //   ,1a,14*0,21,1a,14*0,21,1a,14*0,21,1a,14*0,21,1a,14*0,21,1a,14*0
  //   ,21,1a,14*0,21,1a,14*0,21,1a,14*0,21,1a,14*0,21,1a,14*0,21,1a
  //   ,14*0,21,1a,14*0,21,1a,14*0,21,1a,14*0,21,1a,14*0,21,1a,14*0,21
  //   ,1a,14*0,21,1a,14*0,21,1a,14*0,21,1a,14*0,21,1a,14*0,21,1a,14*0
  //   ,21,1a,8480,800000,12*0,21,1a,14*0,21,1a,14*0,21,1a,14*0,21,1a
  //   ,8c80,800000,12*0,21,1a,14*0,21,1a,14*0,21,1a,14*0,21,1a,14*0
  //   ,21,1a,14*0,21,1a,14*0,21,1a,14*0,21,1a,14*0,21,1a,14*0,21,1a
  //   ,14*0,21,1a,14*0,21,1a,21,4012,800000,11*0,21,1a,14*0,21,1a,14*0
  //   ,21,1a,14*0,21,1a,2,800000,12*0,21,1a,14*0,21,1a,14*0,21,1a,14*0
  //   ,21,1a,800000,13*0,21,1a,14*0,21,1a,14*0,21,1a,14*0,21,1a,14*0
  //   ,21,1a,14*0,21,1a,14*0,21,1a,14*0,21,1a,14*0,21,1a,14*0,21,1a
  //   ,14*0,21,1a,14*0,21,1a,14*0,21,1a,14*0,21,1a,14*0,21,1a,14*0,21
  //   ,1a,14*0,21,1a,14*0,21,1a,14*0,21,1a,14*0,21,1a,14*0,21,1a,14*0
  //   ,21,1a,14*0,21,1a,14*0,21,1a,21,92,800000,11*0,21,1a,14*0,21,1a
  //   ,14*0,21,1a,14*0,21,1a,21,212,800000,11*0,21,1a,14*0,21,1a,14*0
  //   ,21,1a,14*0,21,1a,2040,800000,12*0,21,1a,14*0,21,1a,14*0,21,1a
  //   ,14*0,21,1a,14*0,21,1a,14*0,21,1a,14*0,21,1a,14*0,21,1a,14*0,21
  //   ,1a,14*0,21,1a,14*0,21,1a,14*0,21,1a,14*0,21,1a,14*0,21,1a,14*0
  //   ,21,1a,14*0,21,1a,14*0,21,1a,14*0,21,1a,14*0,21,1a,14*0,21,1a
  //   ,14*0,21,1a,14*0,21,1a,c00000,13*0,21,1a,200000,13*0,21,1a,14*0
  //   ,21,1a,14*0,21,1a,14*0,21,1a,14*0,21,1a,14*0,21,1a,14*0,21,1a
  //   ,14*0,21,1a,14*0,21,1a,14*0,21,1a,14*0,21,1a,14*0,21,1a,14*0,21
  //   ,1a,14*0,21,1a,14*0,21,1a,14*0,21,1a,14*0,21,1a,14*0,21,1a,14*0
  //   ,21,1a,14*0,21,1a,14*0,21,1a,14*0,21,1a,14*0,21,1a,14*0,21,1a
  //   ,14*0,21,1a,14*0,21,1a,14*0,21,1a,14*0,21,1a,14*0,21,1a,14*0,21
  //   ,1a,14*0,21,1a,14*0,21,1a,14*0,21,1a,14*0,21,1a,14*0,21,1a,14*0
  //   ,21,1a,14*0,21,1a,14*0,21,1a,14*0,21,1a,14*0,21,1a,14*0,21,1a
  //   ,14*0,21,1a,14*0,21,1a,14*0,21,1a,14*0,21,1a,14*0,21,1a,14*0,21
  //   ,1a,14*0,21,1a,14*0,21,1a,14*0,21,1a,14*0,21,1a,14*0,21,1a,14*0
  //   ,21,1a,14*0,21,1a,14*0,21,1a,14*0,21,1a,14*0,21,1a,14*0,21,1a
  //   ,14*0,21,1a,14*0,21,1a,14*0,21,1a,14*0,21,1a,14*0,21,1a,14*0,21
  //   ,1a,14*0,21,1a,14*0,21,1a,14*0,21,1a,14*0,21,1a,14*0,21,1a,14*0
  //   ,21,1a,14*0,21,1a,14*0,21,1a,14*0,21,1a,14*0,21,1a,14*0,21,1a
  //   ,14*0,21,1a,14*0,21,1a,14*0,21,1a,14*0,21,1a,14*0,21,1a,14*0,21
  //   ,1a,14*0,21,1a,14*0,21,1a,14*0,21,1a,14*0,21,1a,14*0,21,1a,14*0
  //   ,21,1a,14*0,21,1a,14*0,21,1a,14*0,21,1a,14*0,21,1a,14*0,21,1a
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  //   contents of Microcode_3 (hex, n*v repeats v):
  //   21,1a,14*0,21,1a,14*0,21,1a,14*0,21,1a,14*0,21,1a,14*0,21,1a,14*0
  //   ,21,1a,14*0,21,1a,14*0,21,1a,14*0,21,1a,14*0,21,1a,14*0,21,1a
  //   ,14*0,21,1a,14*0,21,1a,14*0,21,1a,14*0,21,1a,14*0,21,1a,14*0,21
  //   ,1a,14*0,21,1a,14*0,21,1a,14*0,21,1a,14*0,21,1a,14*0,21,1a,14*0
  //   ,21,1a,14*0,21,1a,14*0,21,1a,14*0,21,1a,14*0,21,1a,14*0,21,1a
  //   ,14*0,21,1a,14*0,21,1a,14*0,21,1a,14*0,21,1a,14*0,21,1a,14*0,21
  //   ,1a,14*0,21,1a,14*0,21,1a,14*0,21,1a,14*0,21,1a,14*0,21,1a,14*0
  //   ,21,1a,14*0,21,1a,14*0,21,1a,14*0,21,1a,14*0,21,1a,14*0,21,1a
  //   ,14*0,21,1a,14*0,21,1a,14*0,21,1a,14*0,21,1a,14*0,21,1a,14*0,21
  //   ,1a,14*0,21,1a,14*0,21,1a,14*0,21,1a,14*0,21,1a,14*0,21,1a,14*0
  //   ,21,1a,14*0,21,1a,14*0,21,1a,14*0,21,1a,14*0,21,1a,14*0,21,1a
  //   ,14*0,21,1a,14*0,21,1a,14*0,21,1a,14*0,21,1a,14*0,21,1a,14*0,21
  //   ,1a,14*0,21,1a,14*0,21,1a,14*0,21,1a,14*0,21,1a,14*0,21,1a,14*0
  //   ,21,1a,14*0,21,1a,14*0,21,1a,14*0,21,1a,14*0,21,1a,14*0,21,1a
  //   ,14*0,21,1a,14*0,21,1a,14*0,21,1a,14*0,21,1a,14*0,21,1a,14*0,21
  //   ,1a,14*0,21,1a,14*0,21,1a,14*0,21,1a,14*0,21,1a,14*0,21,1a,14*0
  //   ,21,1a,14*0,21,1a,14*0,21,1a,14*0,21,1a,14*0,21,1a,14*0,21,1a
  //   ,14*0,21,1a,14*0,21,1a,14*0,21,1a,14*0,21,1a,14*0,21,1a,14*0,21
  //   ,1a,14*0,21,1a,14*0,21,1a,14*0,21,1a,14*0,21,1a,14*0,21,1a,14*0
  //   ,21,1a,14*0,21,1a,14*0,21,1a,14*0,21,1a,14*0,21,1a,14*0,21,1a
  //   ,14*0,21,1a,14*0,21,1a,14*0,21,1a,14*0,21,1a,14*0,21,1a,14*0,21
  //   ,1a,14*0,21,1a,14*0,21,1a,14*0,21,1a,14*0,21,1a,14*0,21,1a,14*0
  //   ,21,1a,14*0,21,1a,14*0,21,1a,14*0,21,1a,14*0,21,1a,14*0,21,1a
  //   ,14*0,21,1a,14*0,21,1a,14*0,21,1a,14*0,21,1a,14*0,21,1a,14*0,21
  //   ,1a,14*0,21,1a,14*0,21,1a,14*0,21,1a,14*0,21,1a,14*0,21,1a,14*0
  //   ,21,1a,14*0,21,1a,14*0,21,1a,14*0,21,1a,14*0,21,1a,14*0,21,1a
  //   ,14*0,21,1a,14*0,21,1a,14*0,21,1a,14*0,21,1a,14*0,21,1a,14*0,21
  //   ,1a,14*0,21,1a,14*0,21,1a,14*0,21,1a,14*0,21,1a,14*0,21,1a,14*0
  //   ,21,1a,14*0,21,1a,14*0,21,1a,14*0,21,1a,14*0,21,1a,14*0,21,1a
  //   ,14*0,21,1a,14*0,21,1a,14*0,21,1a,14*0,21,1a,14*0,21,1a,14*0,21
  //   ,1a,14*0,21,1a,14*0,21,1a,14*0,21,1a,14*0,21,1a,14*0,21,1a,14*0
  //   ,21,1a,8480,800000,12*0,21,1a,14*0,21,1a,14*0,21,1a,14*0,21,1a
  //   ,8c80,800000,12*0,21,1a,14*0,21,1a,14*0,21,1a,14*0,21,1a,14*0
  //   ,21,1a,14*0,21,1a,14*0,21,1a,14*0,21,1a,14*0,21,1a,14*0,21,1a
  //   ,14*0,21,1a,14*0,21,1a,21,4012,800000,11*0,21,1a,14*0,21,1a,14*0
  //   ,21,1a,14*0,21,1a,2,800000,12*0,21,1a,14*0,21,1a,14*0,21,1a,14*0
  //   ,21,1a,800000,13*0,21,1a,14*0,21,1a,14*0,21,1a,14*0,21,1a,14*0
  //   ,21,1a,14*0,21,1a,14*0,21,1a,14*0,21,1a,14*0,21,1a,14*0,21,1a
  //   ,14*0,21,1a,14*0,21,1a,14*0,21,1a,14*0,21,1a,14*0,21,1a,14*0,21
  //   ,1a,14*0,21,1a,14*0,21,1a,14*0,21,1a,14*0,21,1a,14*0,21,1a,14*0
  //   ,21,1a,14*0,21,1a,14*0,21,1a,21,92,800000,11*0,21,1a,14*0,21,1a
  //   ,14*0,21,1a,14*0,21,1a,21,212,800000,11*0,21,1a,14*0,21,1a,14*0
  //   ,21,1a,14*0,21,1a,2040,800000,12*0,21,1a,14*0,21,1a,14*0,21,1a
  //   ,14*0,21,1a,14*0,21,1a,14*0,21,1a,14*0,21,1a,14*0,21,1a,14*0,21
  //   ,1a,14*0,21,1a,14*0,21,1a,14*0,21,1a,14*0,21,1a,14*0,21,1a,14*0
  //   ,21,1a,14*0,21,1a,14*0,21,1a,14*0,21,1a,14*0,21,1a,14*0,21,1a
  //   ,14*0,21,1a,14*0,21,1a,c00000,13*0,21,1a,200000,13*0,21,1a,14*0
  //   ,21,1a,14*0,21,1a,14*0,21,1a,14*0,21,1a,14*0,21,1a,14*0,21,1a
  //   ,14*0,21,1a,14*0,21,1a,14*0,21,1a,14*0,21,1a,14*0,21,1a,14*0,21
  //   ,1a,14*0,21,1a,14*0,21,1a,14*0,21,1a,14*0,21,1a,14*0,21,1a,14*0
  //   ,21,1a,14*0,21,1a,14*0,21,1a,14*0,21,1a,14*0,21,1a,14*0,21,1a
  //   ,14*0,21,1a,14*0,21,1a,14*0,21,1a,14*0,21,1a,14*0,21,1a,14*0,21
  //   ,1a,14*0,21,1a,14*0,21,1a,14*0,21,1a,14*0,21,1a,14*0,21,1a,14*0
  //   ,21,1a,14*0,21,1a,14*0,21,1a,14*0,21,1a,14*0,21,1a,14*0,21,1a
  //   ,14*0,21,1a,14*0,21,1a,14*0,21,1a,14*0,21,1a,14*0,21,1a,14*0,21
  //   ,1a,14*0,21,1a,14*0,21,1a,14*0,21,1a,14*0,21,1a,14*0,21,1a,14*0
  //   ,21,1a,14*0,21,1a,14*0,21,1a,14*0,21,1a,14*0,21,1a,14*0,21,1a
  //   ,14*0,21,1a,14*0,21,1a,14*0,21,1a,14*0,21,1a,14*0,21,1a,14*0,21
  //   ,1a,14*0,21,1a,14*0,21,1a,14*0,21,1a,14*0,21,1a,14*0,21,1a,14*0
  //   ,21,1a,14*0,21,1a,14*0,21,1a,14*0,21,1a,14*0,21,1a,14*0,21,1a
  //   ,14*0,21,1a,14*0,21,1a,14*0,21,1a,14*0,21,1a,14*0,21,1a,14*0,21
  //   ,1a,14*0,21,1a,14*0,21,1a,14*0,21,1a,14*0,21,1a,14*0,21,1a,14*0
  //   ,21,1a,14*0,21,1a,14*0,21,1a,14*0,21,1a,14*0,21,1a,14*0,21,1a
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  //   contents of Microcode_4 (hex, n*v repeats v):
  //   21,1a,14*0,21,1a,14*0,21,1a,14*0,21,1a,14*0,21,1a,14*0,21,1a,14*0
  //   ,21,1a,14*0,21,1a,14*0,21,1a,14*0,21,1a,14*0,21,1a,14*0,21,1a
  //   ,14*0,21,1a,14*0,21,1a,14*0,21,1a,14*0,21,1a,14*0,21,1a,14*0,21
  //   ,1a,14*0,21,1a,14*0,21,1a,14*0,21,1a,14*0,21,1a,14*0,21,1a,14*0
  //   ,21,1a,14*0,21,1a,14*0,21,1a,14*0,21,1a,14*0,21,1a,14*0,21,1a
  //   ,14*0,21,1a,14*0,21,1a,14*0,21,1a,14*0,21,1a,14*0,21,1a,14*0,21
  //   ,1a,14*0,21,1a,14*0,21,1a,14*0,21,1a,14*0,21,1a,14*0,21,1a,14*0
  //   ,21,1a,14*0,21,1a,14*0,21,1a,14*0,21,1a,14*0,21,1a,14*0,21,1a
  //   ,14*0,21,1a,14*0,21,1a,14*0,21,1a,14*0,21,1a,14*0,21,1a,14*0,21
  //   ,1a,14*0,21,1a,14*0,21,1a,14*0,21,1a,14*0,21,1a,14*0,21,1a,14*0
  //   ,21,1a,14*0,21,1a,14*0,21,1a,14*0,21,1a,14*0,21,1a,14*0,21,1a
  //   ,14*0,21,1a,14*0,21,1a,14*0,21,1a,14*0,21,1a,14*0,21,1a,14*0,21
  //   ,1a,14*0,21,1a,14*0,21,1a,14*0,21,1a,14*0,21,1a,14*0,21,1a,14*0
  //   ,21,1a,14*0,21,1a,14*0,21,1a,14*0,21,1a,14*0,21,1a,14*0,21,1a
  //   ,14*0,21,1a,14*0,21,1a,14*0,21,1a,14*0,21,1a,14*0,21,1a,14*0,21
  //   ,1a,14*0,21,1a,14*0,21,1a,14*0,21,1a,14*0,21,1a,14*0,21,1a,14*0
  //   ,21,1a,14*0,21,1a,14*0,21,1a,14*0,21,1a,14*0,21,1a,14*0,21,1a
  //   ,14*0,21,1a,14*0,21,1a,14*0,21,1a,14*0,21,1a,14*0,21,1a,14*0,21
  //   ,1a,14*0,21,1a,14*0,21,1a,14*0,21,1a,14*0,21,1a,14*0,21,1a,14*0
  //   ,21,1a,14*0,21,1a,14*0,21,1a,14*0,21,1a,14*0,21,1a,14*0,21,1a
  //   ,14*0,21,1a,14*0,21,1a,14*0,21,1a,14*0,21,1a,14*0,21,1a,14*0,21
  //   ,1a,14*0,21,1a,14*0,21,1a,14*0,21,1a,14*0,21,1a,14*0,21,1a,14*0
  //   ,21,1a,14*0,21,1a,14*0,21,1a,14*0,21,1a,14*0,21,1a,14*0,21,1a
  //   ,14*0,21,1a,14*0,21,1a,14*0,21,1a,14*0,21,1a,14*0,21,1a,14*0,21
  //   ,1a,14*0,21,1a,14*0,21,1a,14*0,21,1a,14*0,21,1a,14*0,21,1a,14*0
  //   ,21,1a,14*0,21,1a,14*0,21,1a,14*0,21,1a,14*0,21,1a,14*0,21,1a
  //   ,14*0,21,1a,14*0,21,1a,14*0,21,1a,14*0,21,1a,14*0,21,1a,14*0,21
  //   ,1a,14*0,21,1a,14*0,21,1a,14*0,21,1a,14*0,21,1a,14*0,21,1a,14*0
  //   ,21,1a,14*0,21,1a,14*0,21,1a,14*0,21,1a,14*0,21,1a,14*0,21,1a
  //   ,14*0,21,1a,14*0,21,1a,14*0,21,1a,14*0,21,1a,14*0,21,1a,14*0,21
  //   ,1a,14*0,21,1a,14*0,21,1a,14*0,21,1a,14*0,21,1a,14*0,21,1a,14*0
  //   ,21,1a,8480,800000,12*0,21,1a,14*0,21,1a,14*0,21,1a,14*0,21,1a
  //   ,8c80,800000,12*0,21,1a,14*0,21,1a,14*0,21,1a,14*0,21,1a,14*0
  //   ,21,1a,14*0,21,1a,14*0,21,1a,14*0,21,1a,14*0,21,1a,14*0,21,1a
  //   ,14*0,21,1a,14*0,21,1a,21,4012,800000,11*0,21,1a,14*0,21,1a,14*0
  //   ,21,1a,14*0,21,1a,2,800000,12*0,21,1a,14*0,21,1a,14*0,21,1a,14*0
  //   ,21,1a,800000,13*0,21,1a,14*0,21,1a,14*0,21,1a,14*0,21,1a,14*0
  //   ,21,1a,14*0,21,1a,14*0,21,1a,14*0,21,1a,14*0,21,1a,14*0,21,1a
  //   ,14*0,21,1a,14*0,21,1a,14*0,21,1a,14*0,21,1a,14*0,21,1a,14*0,21
  //   ,1a,14*0,21,1a,14*0,21,1a,14*0,21,1a,14*0,21,1a,14*0,21,1a,14*0
  //   ,21,1a,14*0,21,1a,14*0,21,1a,21,92,800000,11*0,21,1a,14*0,21,1a
  //   ,14*0,21,1a,14*0,21,1a,21,212,800000,11*0,21,1a,14*0,21,1a,14*0
  //   ,21,1a,14*0,21,1a,2040,800000,12*0,21,1a,14*0,21,1a,14*0,21,1a
  //   ,14*0,21,1a,14*0,21,1a,14*0,21,1a,14*0,21,1a,14*0,21,1a,14*0,21
  //   ,1a,14*0,21,1a,14*0,21,1a,14*0,21,1a,14*0,21,1a,14*0,21,1a,14*0
  //   ,21,1a,14*0,21,1a,14*0,21,1a,14*0,21,1a,14*0,21,1a,14*0,21,1a
  //   ,14*0,21,1a,14*0,21,1a,c00000,13*0,21,1a,200000,13*0,21,1a,14*0
  //   ,21,1a,14*0,21,1a,14*0,21,1a,14*0,21,1a,14*0,21,1a,14*0,21,1a
  //   ,14*0,21,1a,14*0,21,1a,14*0,21,1a,14*0,21,1a,14*0,21,1a,14*0,21
  //   ,1a,14*0,21,1a,14*0,21,1a,14*0,21,1a,14*0,21,1a,14*0,21,1a,14*0
  //   ,21,1a,14*0,21,1a,14*0,21,1a,14*0,21,1a,14*0,21,1a,14*0,21,1a
  //   ,14*0,21,1a,14*0,21,1a,14*0,21,1a,14*0,21,1a,14*0,21,1a,14*0,21
  //   ,1a,14*0,21,1a,14*0,21,1a,14*0,21,1a,14*0,21,1a,14*0,21,1a,14*0
  //   ,21,1a,14*0,21,1a,14*0,21,1a,14*0,21,1a,14*0,21,1a,14*0,21,1a
  //   ,14*0,21,1a,14*0,21,1a,14*0,21,1a,14*0,21,1a,14*0,21,1a,14*0,21
  //   ,1a,14*0,21,1a,14*0,21,1a,14*0,21,1a,14*0,21,1a,14*0,21,1a,14*0
  //   ,21,1a,14*0,21,1a,14*0,21,1a,14*0,21,1a,14*0,21,1a,14*0,21,1a
  //   ,14*0,21,1a,14*0,21,1a,14*0,21,1a,14*0,21,1a,14*0,21,1a,14*0,21
  //   ,1a,14*0,21,1a,14*0,21,1a,14*0,21,1a,14*0,21,1a,14*0,21,1a,14*0
  //   ,21,1a,14*0,21,1a,14*0,21,1a,14*0,21,1a,14*0,21,1a,14*0,21,1a
  //   ,14*0,21,1a,14*0,21,1a,14*0,21,1a,14*0,21,1a,14*0,21,1a,14*0,21
  //   ,1a,14*0,21,1a,14*0,21,1a,14*0,21,1a,14*0,21,1a,14*0,21,1a,14*0
  //   ,21,1a,14*0,21,1a,14*0,21,1a,14*0,21,1a,14*0,21,1a,14*0,21,1a
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  //   I/O-Request if IO or IN are high.
  //   Interrupts masked except in Exec.
  //   Optimized clear TMP-Regs.
  //   Multiplex Input/Output Signals
  //   if not used in parallel.
endmodule
