// Digital circuit Keyboard-Modify.dig as structural Verilog
module Keyboard_Modify (
  input  [15:0] KBDIN,
  output [7:0] KBDOUT
);

  wire lt_LF_gt___eq__0x0A__eq__0001010_eq;

  Comparator #(.Bits(8)) lt_LF_gt___eq__0x0A__eq__0001010 (
    .a(KBDIN[7:0]), .b(8'ha), .eq(lt_LF_gt___eq__0x0A__eq__0001010_eq));  // open: gt, lt
  Multiplexer #(.Bits(8)) multiplexer_1 (
    .sel(lt_LF_gt___eq__0x0A__eq__0001010_eq), .in_0(KBDIN[7:0]), .in_1(8'hd), .out(KBDOUT));

  // Notes on the sheet:
  //   <CR> = 0x0D = 0001101
endmodule
