// Digital circuit TTY.dig as structural Verilog
module TTY (
  input  [7:0] ADDR_L,
  input  SYNC,
  input  IORQ,
  input  IN_nOUT,
  output [7:0] BUS
);

  wire and_2_out, and_3_out, avail, TTY_Data, TTY_Status;
  wire [1:1] and_1_out;
  wire [7:0] dipswitch_2_out, dipswitch_4_out, keyboard_modify_1_kbdout;
  wire [15:0] keyboard_1_d;

  DipSwitch dipswitch_1 (.out(dipswitch_2_out[6]));
  DipSwitch dipswitch_2 (.out(dipswitch_2_out[7]));
  DipSwitch dipswitch_3 (.out(dipswitch_4_out[6]));
  DipSwitch dipswitch_4 (.out(dipswitch_4_out[7]));
  DipSwitch dipswitch_5 (.out(dipswitch_2_out[2]));
  DipSwitch dipswitch_6 (.out(dipswitch_2_out[3]));
  DipSwitch #(.dipDefault("true")) dipswitch_7 (.out(dipswitch_2_out[4]));
  DipSwitch dipswitch_8 (.out(dipswitch_2_out[5]));
  DipSwitch dipswitch_9 (.out(dipswitch_4_out[2]));
  DipSwitch dipswitch_10 (.out(dipswitch_4_out[3]));
  DipSwitch #(.dipDefault("true")) dipswitch_11 (.out(dipswitch_4_out[4]));
  DipSwitch dipswitch_12 (.out(dipswitch_4_out[5]));
  DipSwitch dipswitch_13 (.out(dipswitch_2_out[0]));
  DipSwitch dipswitch_14 (.out(dipswitch_2_out[1]));
  DipSwitch #(.dipDefault("true")) dipswitch_15 (.out(dipswitch_4_out[0]));
  DipSwitch dipswitch_16 (.out(dipswitch_4_out[1]));
  Comparator #(.Bits(8)) comparator_1 (.a(ADDR_L), .b(dipswitch_2_out), .eq(TTY_Status));  // open: gt, lt
  Comparator #(.Bits(8)) comparator_2 (.a(ADDR_L), .b(dipswitch_4_out), .eq(TTY_Data));  // open: gt, lt
  and and_1 (and_1_out[1], TTY_Status, IORQ, IN_nOUT);
  and and_2 (and_2_out, TTY_Data, IORQ, IN_nOUT);
  and and_3 (and_3_out, TTY_Data, IORQ, ~IN_nOUT);  // And
  Keyboard keyboard_1 (.C(SYNC), .en(and_2_out), .D(keyboard_1_d), .av(avail));
  Terminal #(.termWidth(80)) terminal_1 (.D(BUS), .C(SYNC), .en(and_3_out));
  assign BUS = and_1_out[1] ? {{6{1'b0}}, and_1_out[1], avail} : 8'bz;  // Driver driver_1
  Keyboard_Modify keyboard_modify_1 (.KBDIN(keyboard_1_d), .KBDOUT(keyboard_modify_1_kbdout));
  assign BUS = and_2_out ? keyboard_modify_1_kbdout : 8'bz;  // Driver driver_2

  // Other names for the same wires on the sheet: D_in[7:0] = BUS; D_out[7:0] = BUS; Status[7:0] = BUS

  // Notes on the sheet:
  //   Status (0x10)
  //   Data (0x11)
  //   TTY Status
  //   TTY Data
endmodule
